# Fritzing sketch extranfunc (saved by Fritzing 0.9.2b)
breadboards: 1

parts:
  microSD_Transflash1 = SparkFun - microSD Transflash  # not connected
  Part1 = Arduino Uno (Rev3)  # not connected
  R1 = Trimmer Potentiometer [maximum_resistance=10kΩ package=THT]  # not connected
  U1 = LM386 [package=dip08]
  C1 = Tantalum Capacitor [capacitance=10µF package="B 3528 [SMD, tantalum]"]
  C2 = Tantalum Capacitor [capacitance=10µF package="B 3528 [SMD, tantalum]"]
  SPKR1 = Loudspeaker
  C3 = Electrolytic Capacitor [capacitance=0.22mF voltage=35V package="0807 [SMD, electrolytic]"]

nets:
  N1: U1.GAIN, C2.-, C2.+
  N2: U1.OUT, C3.+
  N3: U1.BP, C1.+
  N4: C1.-, SPKR1.pin1
  N5: SPKR1.pin2, C3.-
