# Fritzing sketch BRUNO sensor_and_pushbutton (saved by Fritzing 0.9.2b)
breadboards: 1

parts:
  Part2 = Arduino Uno (Rev3)
  J1 = Basic Servo
  Part3 = SRF05 Ultrasonic Rangefinder
  S1 = Round Pushbutton

nets:
  N1: Part2.D10_PWM/SS, Part3.Echo
  N2: Part2.D11_PWM/MOSI, Part3.Trig
  N3: Part2.D3_PWM, S1.leg1
  N4: Part2.D7, J1.pulse
  VCC: Part2.5V, J1.vcc, Part3.VCC
  GND: Part2.GND, J1.gnd, Part3.GND, S1.leg0
