# Fritzing sketch robot (saved by Fritzing 0.9.2b)
breadboards: 2

parts:
  Part1 = Arduino Uno (Rev3) - ICSP
  Part2 = Arduino Uno (Rev3) - ICSP
  Part3 = Arduino Nano (Rev3.0) (ICSP)
  LCD1 = LCD screen
  U1 = POT [package=3362u]
  R1 = Resistor [tolerance=±5% resistance=220 package="0805 [SMD]"]
  MIC1 = MAX4466_Electret_Microphone_Breakout_Board
  Part4 = SRF05 Ultrasonic Rangefinder
  J1 = Basic Servo
  S1 = Square Pushbutton
  neopixel1 = Neopixel Ring 12
  T1 = LM35 Temperature Sensor [package="TO92 [THT]"]

nets:
  N1: Part1.A0, MIC1.connector1
  N2: Part1.A4/SDA, Part2.A4/SDA, Part3.A4
  N3: Part1.A5/SCL, Part2.A5/SCL, Part3.A5
  N4: Part1.D8, LCD1.RS
  N5: Part1.D9_PWM, LCD1.E
  N6: Part1.D10_PWM/SS, LCD1.DB4
  N7: Part1.D11_PWM/MOSI, LCD1.DB5
  N8: Part1.D12/MISO, LCD1.DB6
  N9: Part1.D13/SCK, LCD1.DB7
  GND: Part1.GND, Part2.GND, Part3.GND, LCD1.VSS, LCD1.R/W, LCD1.LED-, U1.E, MIC1.connector2, Part4.GND, J1.gnd, S1.leg1, neopixel1.GND, T1.GND
  N10: Part1.D3_PWM, R1.Pin_1
  N11: Part1.3V3, MIC1.connector3
  5V: Part1.5V, Part2.5V, Part3.5V, LCD1.VDD, LCD1.LED+, U1.A, Part4.VCC, J1.vcc, neopixel1.VCC, T1.+Vs
  N12: Part2.D8, S1.leg0
  N13: Part2.D9_PWM, J1.pulse
  N14: Part2.D10_PWM/SS, Part4.Echo
  N15: Part2.D11_PWM/MOSI, Part4.Trig
  N16: Part3.A7, T1.Vout
  N17: LCD1.V0, U1.S
  N18: R1.Pin_0, neopixel1.IN

custom parts:
  Neopixel Ring 12: Neopixel Ring x12
