# Fritzing sketch sensors (saved by Fritzing 0.9.2b)
breadboards: 1

parts:
  Part2 = Arduino Uno (Rev3)
  J1 = Basic Servo
  U1 = TMP36 [package=to-92]
  R1 = Resistor [tolerance=±5% resistance=220 package="0402 [SMD]"]
  Part3 = SRF05 Ultrasonic Rangefinder

nets:
  N1: Part2.A1, U1.VOUT
  N2: Part2.A2, Part3.Echo
  N3: Part2.D9_PWM, J1.pulse
  N4: Part2.D10_PWM/SS, Part3.Trig
  GND: Part2.GND, J1.gnd, R1.Pin_0
  VCC: J1.vcc, U1.VCC
  N5: U1.GND, R1.Pin_1
